// Logisim project cpu.circ as structural Verilog: 1 circuit, main circuit cpu
module cpu (
  input  Rest
);

  wire alu_1_zero, alucontroller_1_sh_amount, and_1_out, and_2_out, and_3_out, and_4_out, and_5_out, clk,
       comparator_1_eq, main_1_alusrc, main_1_branch, main_1_jump, main_1_memtoreg, main_1_regdst,
       main_1_regwren, multiplexer_2_out, not_1_out, RType;
  wire [3:0] adder_1_out_2, main_1_memwrmask;
  wire [4:0] alucontroller_1_alu_out, InstMem_memreaddata_2, InstMem_memreaddata_3, multiplexer_3_out,
       multiplexer_4_out;
  wire [5:0] InstMem_memreaddata;
  wire [25:16] InstMem_memreaddata_4;
  wire [27:0] adder_1_out;
  wire [31:0] adder_2_out, alu_1_result, bit_extender_1_out, bit_extender_2_out, bit_extender_3_out,
       DataMem_memreaddata, multiplexer_1_out, multiplexer_5_out, multiplexer_6_out, multiplexer_7_out,
       multiplexer_8_out, multiplexer_9_out, multiplexer_10_out, pc, RegisterFile_p7, RegisterFile_p8,
       shifter_1_out, shifter_2_out, shifter_3_out, signextend_1_extended, xor_1_out;
  wire [31:26] InstMem_memreaddata_5;

  Multiplexer #(.width(32)) multiplexer_1 (
    .in0(multiplexer_9_out), .in1(alu_1_result), .out(multiplexer_1_out), .sel(and_3_out));
  Multiplexer multiplexer_2 (.in0(1'b1), .in1(1'b0), .out(multiplexer_2_out), .sel(and_4_out));
  Clock u_Clk (.out(clk));
  Register #(.trigger("falling"), .width(32)) u_PC (
    .D(multiplexer_1_out), .en(multiplexer_2_out), .clk(clk), .Q(pc), .clr(Rest));
  Adder #(.width(32)) adder_1 (.a(32'h4), .b(pc), .out({adder_1_out_2, adder_1_out}));  // open: cin, cout
  mem InstMem (
    .MemAddress(pc), .clk(clk),
    .MemReadData({InstMem_memreaddata_5, InstMem_memreaddata_4, InstMem_memreaddata_3, InstMem_memreaddata_2, InstMem_memreaddata}));  // open: MemWriteMask, MemWriteData
  Multiplexer #(.width(5)) multiplexer_3 (
    .in0(InstMem_memreaddata_4[20:16]), .in1(InstMem_memreaddata_3), .out(multiplexer_3_out),
    .sel(main_1_regdst));
  assign bit_extender_1_out = {{6{1'b0}}, {InstMem_memreaddata_4, InstMem_memreaddata_3, InstMem_memreaddata_2, InstMem_memreaddata}};  // Bit_Extender bit_extender_1
  and and_1 (and_1_out, main_1_jump, main_1_regwren);
  Multiplexer #(.width(5)) multiplexer_4 (
    .in0(multiplexer_3_out), .in1({5{1'b1}}), .out(multiplexer_4_out), .sel(and_1_out));
  Multiplexer #(.width(32)) multiplexer_5 (
    .in0(multiplexer_10_out), .in1(pc), .out(multiplexer_5_out), .sel(and_1_out));
  Shifter #(.width(32)) shifter_1 (.in(bit_extender_1_out), .\dist (5'b00010), .out(shifter_1_out));
  assign bit_extender_2_out = {{28{1'b0}}, adder_1_out_2};  // Bit_Extender bit_extender_2
  assign bit_extender_3_out = {{27{1'b0}}, InstMem_memreaddata_2};  // Bit_Extender bit_extender_3
  Shifter #(.width(32)) shifter_2 (.in(bit_extender_2_out), .\dist (5'b11100), .out(shifter_2_out));
  Control_main main_1 (
    .Opcode(InstMem_memreaddata_5), .RegDst(main_1_regdst), .Branch(main_1_branch), .Jump(main_1_jump),
    .RegWrEn(main_1_regwren), .AluSrc(main_1_alusrc), .MemToReg(main_1_memtoreg), .AluOpr(RType),
    .MemWrMask(main_1_memwrmask));
  assign xor_1_out = shifter_1_out ^ shifter_2_out;  // XOR_Gate xor_1, 32 bits wide
  // regfile RegisterFile: pin names not known; wires that end beside it: InstMem_memreaddata_4[25:21], InstMem_memreaddata_4[20:16], multiplexer_4_out, multiplexer_5_out, main_1_regwren, clk, RegisterFile_p7, RegisterFile_p8
  signExtend signextend_1 (
    .Immd({InstMem_memreaddata_3, InstMem_memreaddata_2, InstMem_memreaddata}),
    .Extended(signextend_1_extended));
  and and_2 (and_2_out, ~main_1_branch, main_1_alusrc);  // AND_Gate
  Multiplexer #(.width(32)) multiplexer_6 (
    .in0(RegisterFile_p7), .in1(bit_extender_3_out), .out(multiplexer_6_out), .sel(alucontroller_1_sh_amount));
  Shifter #(.width(32)) shifter_3 (.in(signextend_1_extended), .\dist (5'b00010), .out(shifter_3_out));
  Multiplexer #(.width(32)) multiplexer_7 (
    .in0(RegisterFile_p8), .in1(signextend_1_extended), .out(multiplexer_7_out), .sel(and_2_out));
  AluController alucontroller_1 (
    .func(InstMem_memreaddata), .opcode(InstMem_memreaddata_5), .aluOperation(RType),
    .ALU_out(alucontroller_1_alu_out), .sh_amount(alucontroller_1_sh_amount));
  and and_3 (and_3_out, alu_1_zero, ~comparator_1_eq, RType);  // AND_Gate
  Adder #(.width(32)) adder_2 (
    .a({adder_1_out_2, adder_1_out}), .b(shifter_3_out), .out(adder_2_out));  // open: cin, cout
  and and_4 (and_4_out, RType, alu_1_zero, comparator_1_eq);
  ALU alu_1 (
    .ReadData1(multiplexer_6_out), .ReadData2(multiplexer_7_out), .ControlBits(alucontroller_1_alu_out),
    .Result(alu_1_result), .Zero(alu_1_zero));
  Multiplexer #(.width(32)) multiplexer_8 (
    .in0({adder_1_out_2, adder_1_out}), .in1(adder_2_out), .out(multiplexer_8_out), .sel(and_5_out));
  and and_5 (and_5_out, main_1_branch, alu_1_zero);
  Multiplexer #(.width(32)) multiplexer_9 (
    .in0(xor_1_out), .in1(multiplexer_8_out), .out(multiplexer_9_out), .sel(not_1_out));
  not not_1 (not_1_out, main_1_jump);
  Comparator #(.width(32)) comparator_1 (.a(alu_1_result), .b({32{1'b1}}), .eq(comparator_1_eq));  // open: gt, lt
  mem DataMem (
    .MemAddress(alu_1_result), .MemWriteMask(main_1_memwrmask), .MemWriteData(RegisterFile_p8), .clk(clk),
    .MemReadData(DataMem_memreaddata));
  Multiplexer #(.width(32)) multiplexer_10 (
    .in0(alu_1_result), .in1(DataMem_memreaddata), .out(multiplexer_10_out), .sel(main_1_memtoreg));
endmodule
